# Fritzing sketch Untitled Sketch (saved by Fritzing 0.8.7b)
breadboards: 1

parts:
  Onderdeel1 = Arduino Uno (Rev3)
  KEYPAD1 = Membrane Matrix Keypad
  R1 = Resistor [tolerance=±5% resistance=220 package=THT]
  LED1 = LED - 5mm [color="Red (633nm)" package="5 mm [THT]"]
  RGB_LED_RING = female pin header, 3 pins [form="♀ (female)"]
  IC1 = IC, DIP package, 8 pins [chip_label=RFID]

nets:
  N1: Onderdeel1.A0, KEYPAD1.5
  N2: Onderdeel1.A1, KEYPAD1.6
  N3: Onderdeel1.A2, KEYPAD1.7
  N4: Onderdeel1.A3, KEYPAD1.1
  N5: Onderdeel1.D8, RGB_LED_RING.pin1
  N6: Onderdeel1.D9_PWM, IC1.pin3
  N7: Onderdeel1.D10_PWM/SS, IC1.pin4
  N8: Onderdeel1.D11_PWM/MOSI, IC1.pin8
  N9: Onderdeel1.D12/MISO, IC1.pin7
  N10: Onderdeel1.D13/SCK, IC1.pin6
  N11: Onderdeel1.GND, LED1.cathode, RGB_LED_RING.pin3, IC1.pin5
  N12: Onderdeel1.A4/SDA, KEYPAD1.2
  N13: Onderdeel1.A5/SCL, KEYPAD1.3
  N14: Onderdeel1.D3_PWM, R1.Pin_0
  N15: Onderdeel1.D7, KEYPAD1.4
  N16: Onderdeel1.3V3, RGB_LED_RING.pin2, IC1.pin1
  N17: R1.Pin_1, LED1.anode

custom parts:
  Membrane Matrix Keypad: Membrane Matrix 3x4 Keypad
